// Logisim project 4_bit_parallel_adder.circ as structural Verilog: 1 circuit, main circuit 4_bit_parallel_adder
// 4_bit_adder
module _4_bit_parallel_adder (
  input  C0,
  input  [3:0] X,
  input  [3:0] Y,
  output S4,
  output S3,
  output S2,
  output S1,
  output G4_star,
  output C4,
  output P4_star
);

  wire and_1_out, and_2_out, and_3_out, and_4_out, and_6_out, and_7_out, and_8_out, and_9_out, and_10_out,
       and_11_out, and_13_out, and_14_out, and_15_out, or_2_out, or_3_out, or_4_out;
  wire [3:0] and_5_out, xor_4_out;

  and and_1 (and_1_out, xor_4_out[3], and_5_out[2]);
  and and_2 (and_2_out, xor_4_out[3], xor_4_out[2], and_5_out[1]);
  xor xor_1 (S4, xor_4_out[3], or_2_out);
  or or_1 (C4, and_5_out[3], and_1_out, and_2_out, and_3_out, and_4_out);
  and and_3 (and_3_out, xor_4_out[3], xor_4_out[2], xor_4_out[1], and_5_out[0]);
  and and_4 (and_4_out, xor_4_out[3], xor_4_out[2], xor_4_out[1], xor_4_out[0], C0);
  assign and_5_out = X & Y;  // AND_Gate and_5, 4 bits wide
  and and_6 (and_6_out, xor_4_out[2], and_5_out[1]);
  xor xor_2 (S3, xor_4_out[2], or_3_out);
  and and_7 (and_7_out, xor_4_out[2], xor_4_out[1], and_5_out[0]);
  or or_2 (or_2_out, and_5_out[2], and_6_out, and_7_out, and_8_out);
  and and_8 (and_8_out, xor_4_out[2], xor_4_out[1], xor_4_out[0], C0);
  xor xor_3 (S2, xor_4_out[1], or_4_out);
  and and_9 (and_9_out, xor_4_out[1], and_5_out[0]);
  or or_3 (or_3_out, and_5_out[1], and_9_out, and_10_out);
  assign xor_4_out = X ^ Y;  // XOR_Gate xor_4, 4 bits wide
  and and_10 (and_10_out, xor_4_out[1], xor_4_out[0], C0);
  xor xor_5 (S1, xor_4_out[0], C0);
  or or_4 (or_4_out, and_5_out[0], and_11_out);
  and and_11 (and_11_out, xor_4_out[0], C0);
  and and_12 (P4_star, xor_4_out[0], xor_4_out[1], xor_4_out[2], xor_4_out[3]);
  and and_13 (and_13_out, xor_4_out[1], xor_4_out[2], xor_4_out[3], and_5_out[0]);
  or or_5 (G4_star, and_13_out, and_14_out, and_15_out, and_5_out[3]);
  and and_14 (and_14_out, xor_4_out[2], xor_4_out[3], and_5_out[1]);
  and and_15 (and_15_out, xor_4_out[3], and_5_out[2]);
endmodule
