// Logisim project CS1409_U201414797_张丹朱_alu.circ as structural Verilog: 6 circuits, main circuit ALU
module ALU (
  input  [31:0] X,
  input  [31:0] Y,
  input  [3:0] AluOP,
  output Signed_Overflow,
  output UnSigned_Overflow,
  output Equal,
  output [31:0] Result,
  output [31:0] Result_2
);

  wire comparator_1_lt, comparator_2_lt, n32_bit_adder_1_of, n32_bit_adder_1_uof, n32_bit_adder_2_of,
       n32_bit_adder_2_uof;
  wire [31:0] and_1_out, bit_extender_1_out, bit_extender_2_out, divider_1_out, divider_1_rem,
       multiplier_1_cout, multiplier_1_out, n32_bit_adder_1_out, n32_bit_adder_2_out, not_1_out, not_2_out,
       or_1_out, shifter_1_out, shifter_2_out, shifter_3_out, xor_1_out;

  // Probe on X
  // Probe on X
  // Probe on Y
  // Probe on Y
  assign not_1_out = ~Y;  // NOT_Gate not_1, 32 bits wide
  Shifter #(.width(32)) shifter_1 (.in(X), .\dist (Y[4:0]), .out(shifter_1_out));
  Shifter #(.width(32), .shift("ar")) shifter_2 (.in(X), .\dist (Y[4:0]), .out(shifter_2_out));
  Shifter #(.width(32), .shift("lr")) shifter_3 (.in(X), .\dist (Y[4:0]), .out(shifter_3_out));
  Multiplier #(.width(32)) multiplier_1 (
    .a(X), .b(Y), .out(multiplier_1_out), .cin({32{1'b0}}), .cout(multiplier_1_cout));
  Divider #(.width(32)) divider_1 (.a(X), .b(Y), .out(divider_1_out), .upper({32{1'b0}}), .rem(divider_1_rem));
  _32_bit_adder u_32_bit_adder_1 (
    .C0(1'b0), .X(X), .Y(Y), .out(n32_bit_adder_1_out), .UOF(n32_bit_adder_1_uof), .OF(n32_bit_adder_1_of));
  _32_bit_adder u_32_bit_adder_2 (
    .C0(1'b1), .X(X), .Y(not_1_out), .out(n32_bit_adder_2_out), .UOF(n32_bit_adder_2_uof),
    .OF(n32_bit_adder_2_of));
  assign and_1_out = X & Y;  // AND_Gate and_1, 32 bits wide
  assign or_1_out = X | Y;  // OR_Gate or_1, 32 bits wide
  assign xor_1_out = X ^ Y;  // XOR_Gate xor_1, 32 bits wide
  assign not_2_out = ~or_1_out;  // NOT_Gate not_2, 32 bits wide
  Comparator #(.width(32)) comparator_1 (.a(X), .b(Y), .lt(comparator_1_lt));  // open: gt, eq
  Comparator #(.width(32), .mode("unsigned")) comparator_2 (
    .a(X), .b(Y), .eq(Equal), .lt(comparator_2_lt));  // open: gt
  // Probe on AluOP
  assign bit_extender_1_out = {{31{1'b0}}, comparator_1_lt};  // Bit_Extender bit_extender_1
  assign bit_extender_2_out = {{31{1'b0}}, comparator_2_lt};  // Bit_Extender bit_extender_2
  // Probe on Result
  // Probe on Result
  // Probe on Result_2
  Multiplexer #(.select(4), .width(32), .enable("false")) multiplexer_1 (
    .in0(shifter_1_out), .in1(shifter_2_out), .in2(shifter_3_out), .in3(multiplier_1_out),
    .in4(divider_1_out), .in5(n32_bit_adder_1_out), .in6(n32_bit_adder_2_out), .in7(and_1_out),
    .in8(or_1_out), .in9(xor_1_out), .in10(not_2_out), .in11(bit_extender_1_out), .in12(bit_extender_2_out),
    .in13({32{1'b0}}), .in14({32{1'b0}}), .in15({32{1'b0}}), .out(Result), .sel(AluOP));
  Multiplexer #(.select(4), .width(32), .enable("false")) multiplexer_2 (
    .in0({32{1'b0}}), .in1({32{1'b0}}), .in2({32{1'b0}}), .in3(multiplier_1_cout), .in4(divider_1_rem),
    .in5({32{1'b0}}), .in6({32{1'b0}}), .in7({32{1'b0}}), .in8({32{1'b0}}), .in9({32{1'b0}}),
    .in10({32{1'b0}}), .in11({32{1'b0}}), .in12({32{1'b0}}), .in13({32{1'b0}}), .in14({32{1'b0}}),
    .in15({32{1'b0}}), .out(Result_2), .sel(AluOP));
  Multiplexer #(.select(4), .enable("false")) multiplexer_3 (
    .in0(1'b0), .in1(1'b0), .in2(1'b0), .in3(1'b0), .in4(1'b0), .in5(n32_bit_adder_1_of),
    .in6(n32_bit_adder_2_of), .in7(1'b0), .in8(1'b0), .in9(1'b0), .in10(1'b0), .in11(1'b0), .in12(1'b0),
    .in13(1'b0), .in14(1'b0), .in15(1'b0), .out(Signed_Overflow), .sel(AluOP));
  Multiplexer #(.select(4), .enable("false")) multiplexer_4 (
    .in0(1'b0), .in1(1'b0), .in2(1'b0), .in3(1'b0), .in4(1'b0), .in5(n32_bit_adder_1_uof),
    .in6(n32_bit_adder_2_uof), .in7(1'b0), .in8(1'b0), .in9(1'b0), .in10(1'b0), .in11(1'b0), .in12(1'b0),
    .in13(1'b0), .in14(1'b0), .in15(1'b0), .out(UnSigned_Overflow), .sel(AluOP));

  // Other names for the same wires on the sheet: OF = Signed_Overflow; Result2[31:0] = Result_2; S[3:0] = AluOP;
  //   UOF = UnSigned_Overflow

  // Notes on the sheet:
  //   不要改变此引脚区域内容，也不要改变ALU封装形式
  //   输入引脚
  //   请在下方利用上方输入输出引脚的隧道信号构建ALU电路，ctrl+d复制选择部件
  //   华中科技大学计算机学院 计算机组成原理，鸣谢加州大学伯克利CS61C课程
  //   输出引脚
  //   探测区域
endmodule

module \演示电路  (
  input  [31:0] X,
  input  [31:0] Y,
  input  [3:0] ALUOP,
  output Signed_Overflow,
  output Unsigned_overflow,
  output [31:0] Result,
  output [31:0] Result_2,
  output Equal
);

  // Probe on X
  // Probe on X
  ALU alu_1 (
    .AluOP(ALUOP), .X(X), .Equal(Equal), .Result(Result), .Signed_Overflow(Signed_Overflow), .Y(Y),
    .Result_2(Result_2), .UnSigned_Overflow(Unsigned_overflow));
  // Probe on ALUOP
  // Probe on Y
  // Probe on Y
  // Probe on Result
  // Probe on Result
  // Probe on Result_2

  // Notes on the sheet:
  //   ALu电路无需调整位置即可连接在该电路中，并且不能出现蓝色线缆和三态输出
endmodule

module \等差数列  (
  input  [31:0] \数列初始值 ,
  input  [31:0] \等差值 ,
  input  \时钟 ,
  output [31:0] Result
);

  // Probe on \数列初始值 
  // Probe on \数列初始值 
  // Probe on \等差值 
  // Probe on \等差值 
  // Probe on Result
  // Probe on Result

  // Other names for the same wires on the sheet: 数列初值[31:0] = \数列初始值 ; 累加和[31:0] = Result

  // Notes on the sheet:
  //   不要改变此引脚区域内容，也不要改变ALU封装形式
  //   请在下方利用上方输入输出引脚的隧道信号构建等差数列求和电路，ctrl+d复制选择部件
  //   华中科技大学计算机学院 计算机组成原理，鸣谢加州大学伯克利CS61C课程
  //   输出引脚
  //   探测区域
endmodule

module CLA (
  input  C0,
  input  G4,
  input  P4,
  input  G3,
  input  P3,
  input  G2,
  input  P2,
  input  G1,
  input  p1,
  output G4_star,
  output P4_star,
  output C4,
  output C3,
  output C2,
  output C1
);

  wire and_1_out, and_2_out, and_3_out, and_5_out, and_6_out, and_7_out, and_8_out, and_9_out, and_10_out,
       and_11_out, and_12_out, and_13_out, and_14_out;

  and and_1 (and_1_out, P4, G3);
  or or_1 (G4_star, G4, and_1_out, and_2_out, and_3_out);
  and and_2 (and_2_out, P4, P3, G2);
  and and_3 (and_3_out, P4, P3, P2, G1);
  and and_4 (P4_star, P4, P3, P2, p1);
  or or_2 (C4, G4, and_5_out, and_6_out, and_7_out, and_8_out);
  and and_5 (and_5_out, P4, G3);
  and and_6 (and_6_out, P4, P3, G2);
  and and_7 (and_7_out, P4, P3, P2, G1);
  and and_8 (and_8_out, P4, P3, P2, p1, C0);
  and and_9 (and_9_out, P3, G2);
  or or_3 (C3, G3, and_9_out, and_11_out, and_10_out);
  and and_10 (and_10_out, P3, P2, p1, C0);
  and and_11 (and_11_out, P3, P2, G1);
  or or_4 (C2, G2, and_13_out, and_12_out);
  and and_12 (and_12_out, P2, p1, C0);
  and and_13 (and_13_out, P2, G1);
  or or_5 (C1, G1, and_14_out);
  and and_14 (and_14_out, p1, C0);
endmodule

module _4_bit_adder (
  input  C0,
  input  [3:0] X,
  input  [3:0] Y,
  output G4_star,
  output P4_star,
  output C4,
  output OF,
  output [3:0] S
);

  wire cla_1_c1, cla_1_c2, cla_1_c3;
  wire [3:0] and_1_out, xor_6_out;

  xor xor_1 (OF, C4, cla_1_c3);
  xor xor_2 (S[3], xor_6_out[3], cla_1_c3);
  assign and_1_out = X & Y;  // AND_Gate and_1, 4 bits wide
  xor xor_3 (S[2], xor_6_out[2], cla_1_c2);
  xor xor_4 (S[1], xor_6_out[1], cla_1_c1);
  CLA cla_1 (
    .C0(C0), .G4_star(G4_star), .P4_star(P4_star), .C4(C4), .C3(cla_1_c3), .C2(cla_1_c2), .C1(cla_1_c1),
    .G4(and_1_out[3]), .P4(xor_6_out[3]), .G3(and_1_out[2]), .P3(xor_6_out[2]), .G2(and_1_out[1]),
    .P2(xor_6_out[1]), .G1(and_1_out[0]), .p1(xor_6_out[0]));
  xor xor_5 (S[0], xor_6_out[0], C0);
  assign xor_6_out = X ^ Y;  // XOR_Gate xor_6, 4 bits wide
endmodule

module _32_bit_adder (
  input  C0,
  input  [31:0] X,
  input  [31:0] Y,
  output UOF,
  output [31:0] out,
  output OF
);

  wire cla_1_c1, cla_1_c2, cla_1_c3, cla_2_c1, cla_3_c1, cla_3_c2, cla_3_c3, cla_3_g4_star, cla_3_p4_star,
       n4_bit_adder_1_c4, n4_bit_adder_1_g4_star, n4_bit_adder_1_p4_star, n4_bit_adder_2_g4_star,
       n4_bit_adder_2_p4_star, n4_bit_adder_3_g4_star, n4_bit_adder_3_p4_star, n4_bit_adder_4_g4_star,
       n4_bit_adder_4_p4_star, n4_bit_adder_5_g4_star, n4_bit_adder_5_p4_star, n4_bit_adder_6_g4_star,
       n4_bit_adder_6_p4_star, n4_bit_adder_7_g4_star, n4_bit_adder_7_p4_star, n4_bit_adder_8_g4_star,
       n4_bit_adder_8_p4_star;

  xor xor_1 (UOF, C0, n4_bit_adder_1_c4);
  _4_bit_adder u_4_bit_adder_1 (
    .C4(n4_bit_adder_1_c4), .C0(cla_1_c3), .G4_star(n4_bit_adder_1_g4_star),
    .P4_star(n4_bit_adder_1_p4_star), .X(X[31:28]), .Y(Y[31:28]), .S(out[31:28]), .OF(OF));
  _4_bit_adder u_4_bit_adder_2 (
    .C0(cla_1_c2), .G4_star(n4_bit_adder_2_g4_star), .P4_star(n4_bit_adder_2_p4_star), .X(X[27:24]),
    .Y(Y[27:24]), .S(out[27:24]));  // open: C4, OF
  CLA cla_1 (
    .C0(cla_2_c1), .C3(cla_1_c3), .C2(cla_1_c2), .C1(cla_1_c1), .G4(n4_bit_adder_1_g4_star),
    .P4(n4_bit_adder_1_p4_star), .G3(n4_bit_adder_2_g4_star), .P3(n4_bit_adder_2_p4_star),
    .G2(n4_bit_adder_3_g4_star), .P2(n4_bit_adder_3_p4_star), .G1(n4_bit_adder_4_g4_star),
    .p1(n4_bit_adder_4_p4_star));  // open: G4_star, P4_star, C4
  _4_bit_adder u_4_bit_adder_3 (
    .C0(cla_1_c1), .G4_star(n4_bit_adder_3_g4_star), .P4_star(n4_bit_adder_3_p4_star), .X(X[23:20]),
    .Y(Y[23:20]), .S(out[23:20]));  // open: C4, OF
  _4_bit_adder u_4_bit_adder_4 (
    .C0(cla_2_c1), .G4_star(n4_bit_adder_4_g4_star), .P4_star(n4_bit_adder_4_p4_star), .X(X[19:16]),
    .Y(Y[19:16]), .S(out[19:16]));  // open: C4, OF
  CLA cla_2 (
    .C0(C0), .C1(cla_2_c1), .G4(1'b0), .P4(1'b0), .G3(1'b0), .P3(1'b0), .G2(1'b0), .P2(1'b0),
    .G1(cla_3_g4_star), .p1(cla_3_p4_star));  // open: G4_star, P4_star, C4, C3, C2
  _4_bit_adder u_4_bit_adder_5 (
    .C0(cla_3_c3), .G4_star(n4_bit_adder_5_g4_star), .P4_star(n4_bit_adder_5_p4_star), .X(X[15:12]),
    .Y(Y[15:12]), .S(out[15:12]));  // open: C4, OF
  _4_bit_adder u_4_bit_adder_6 (
    .C0(cla_3_c2), .G4_star(n4_bit_adder_6_g4_star), .P4_star(n4_bit_adder_6_p4_star), .X(X[11:8]),
    .Y(Y[11:8]), .S(out[11:8]));  // open: C4, OF
  CLA cla_3 (
    .C0(C0), .G4_star(cla_3_g4_star), .P4_star(cla_3_p4_star), .C3(cla_3_c3), .C2(cla_3_c2), .C1(cla_3_c1),
    .G4(n4_bit_adder_5_g4_star), .P4(n4_bit_adder_5_p4_star), .G3(n4_bit_adder_6_g4_star),
    .P3(n4_bit_adder_6_p4_star), .G2(n4_bit_adder_7_g4_star), .P2(n4_bit_adder_7_p4_star),
    .G1(n4_bit_adder_8_g4_star), .p1(n4_bit_adder_8_p4_star));  // open: C4
  _4_bit_adder u_4_bit_adder_7 (
    .C0(cla_3_c1), .G4_star(n4_bit_adder_7_g4_star), .P4_star(n4_bit_adder_7_p4_star), .X(X[7:4]),
    .Y(Y[7:4]), .S(out[7:4]));  // open: C4, OF
  _4_bit_adder u_4_bit_adder_8 (
    .C0(C0), .G4_star(n4_bit_adder_8_g4_star), .P4_star(n4_bit_adder_8_p4_star), .X(X[3:0]), .Y(Y[3:0]),
    .S(out[3:0]));  // open: C4, OF
endmodule
